# Fritzing sketch Schematic (saved by Fritzing 0.9.3b)
breadboards: 2

parts:
  U1 = NodeMCU V1.0
  WeMos_D1_Mini1 = WeMos D1 Mini  # not connected
  S1 = Momentary Switch [package=ksa_sealed_tac_switch]
  S2 = Momentary Switch [package=ksa_sealed_tac_switch]
  DHT1 = DHT11 Humitidy and Temperature Sensor
  DHT2 = DHT11 Humitidy and Temperature Sensor
  R1 = Photocell (LDR) [package=THT]
  R2 = Photocell (LDR) [package=THT]
  R3 = Resistor [tolerance=±5% resistance=10k package="2512 [SMD]"]
  R4 = Resistor [tolerance=±5% resistance=10k package="2512 [SMD]"]

nets:
  N1: U1.D3, S2.1
  3V3: U1.3V3, DHT1.VDD, R2.pin_0
  GND: U1.GND, S2.3, DHT1.GND, R4.Pin_0
  N2: U1.D5, DHT1.DATA
  N3: U1.A0, R2.pin_1, R4.Pin_1
  N4: S1.3, DHT2.GND, R3.Pin_0
  N5: DHT2.VDD, R1.pin_0
  N6: R1.pin_1, R3.Pin_1

custom parts:
  NodeMCU V1.0: ESP8266 based NodeMCU
  WeMos D1 Mini: The D1 mini is a mini wifi board based on ESP-8266EX.
  DHT11 Humitidy and Temperature Sensor: DHT11 Humidity and Temperature Sensor
